// Logisim project example1.circ as structural Verilog: 1 circuit, main circuit main
module main (
  input  X,
  input  Y,
  input  in_3,
  input  in_4,
  input  [15:0] in_5,
  input  [15:0] in_6,
  output [3:0] Z,
  output [15:0] out_8,
  output [15:0] out_9,
  output out_10,
  output [15:0] out_11,
  output [15:0] out_12
);

  wire not_1_out, not_2_out;
  wire [15:0] not_3_out, not_4_out;

  not not_1 (not_1_out, X);
  not not_2 (not_2_out, Y);
  LedBar ledbar_1 (.led0(in_4), .led3(in_4));  // open: led1, led2, led4, led5, led6, led7
  assign not_3_out = ~in_5;  // NOT_Gate not_3, 16 bits wide
  assign not_4_out = ~in_6;  // NOT_Gate not_4, 16 bits wide
  // Probe on not_2_out
  // Probe on X
  LED led_1 (.in(in_3));
  // Probe on not_4_out
  // Probe on in_5
  and and_1 (Z[0], not_2_out, not_1_out);
  and and_2 (Z[1], Y, not_1_out);
  and and_3 (Z[2], not_2_out, X);
  and and_4 (Z[3], X, Y);
  assign out_8 = not_4_out & not_3_out;  // AND_Gate and_5, 16 bits wide
  assign out_9 = in_6 & not_3_out;  // AND_Gate and_6, 16 bits wide
  assign out_11 = not_4_out & in_5;  // AND_Gate and_7, 16 bits wide
  assign out_12 = in_5 & in_6;  // AND_Gate and_8, 16 bits wide
endmodule
