// Logisim project example2.circ as structural Verilog: 3 circuits, main circuit main
module main (
  input  [15:0] A,
  input  [15:0] B,
  input  [15:0] C,
  output [20:0] Z
);

  wire adder_1_cout, adder_2_cout, adder_3_cout, adder_3_out, adder_4_cout, adder_5_cout;
  wire [16:0] shift2_1_o;
  wire [17:0] adder_1_out, adder_2_out, shift4_1_o, shift4_2_o;

  Shift2 shift2_1 (.I(A), .O(shift2_1_o));
  Shift4 shift4_1 (.I(B), .O(shift4_1_o));
  Shift4 shift4_2 (.I(C), .O(shift4_2_o));
  Adder #(.width(18)) adder_1 (.a(shift4_1_o), .b({2'b00, B}), .out(adder_1_out), .cout(adder_1_cout));  // open: cin
  Adder #(.width(18)) adder_2 (
    .a({1'b0, shift2_1_o}), .b(shift4_2_o), .out(adder_2_out), .cout(adder_2_cout));  // open: cin
  Adder #(.width(1)) adder_3 (.a(adder_2_cout), .b(adder_1_cout), .out(adder_3_out), .cout(adder_3_cout));  // open: cin
  Adder #(.width(18)) adder_4 (.a(adder_2_out), .b(adder_1_out), .out(Z[17:0]), .cout(adder_4_cout));  // open: cin
  Adder #(.width(1)) adder_5 (.a(adder_4_cout), .b(adder_3_out), .out(Z[18]), .cout(adder_5_cout));  // open: cin
  Adder #(.width(1)) adder_6 (.a(adder_5_cout), .b(adder_3_cout), .out(Z[19]), .cout(Z[20]));  // open: cin
endmodule

module Shift2 (
  input  [15:0] I,
  output [16:0] O
);


  assign O = {I, 1'b0};
endmodule

module Shift4 (
  input  [15:0] I,
  output [17:0] O
);

  // Probe on 2'b00

  assign O = {I, 2'b00};
endmodule
