// Logisim project da2_task1.circ as structural Verilog: 17 circuits, main circuit DUT
module DUT (
  input  X,
  input  CLK,
  input  RST,
  output Z
);

  wire t0_logic_1_t0_next_input, T0_q, t1_logic_1_t1_next_input, T1_q, t2_logic_1_t2_next_input, T2_q,
       t3_logic_1_t3_next_input, T3_q;

  T0_LOGIC t0_logic_1 (
    .Q3(T3_q), .Q2(T2_q), .Q1(T1_q), .Q0(T0_q), .X(X), .RESET(RST), .T0_NEXT_INPUT(t0_logic_1_t0_next_input));
  T1_LOGIC t1_logic_1 (
    .Q3(T3_q), .Q2(T2_q), .Q1(T1_q), .Q0(T0_q), .X(X), .RESET(RST), .T1_NEXT_INPUT(t1_logic_1_t1_next_input));
  T2_LOGIC t2_logic_1 (
    .Q3(T3_q), .Q2(T2_q), .Q1(T1_q), .Q0(T0_q), .X(X), .RESET(RST), .T2_NEXT_INPUT(t2_logic_1_t2_next_input));
  T3_LOGIC t3_logic_1 (
    .Q3(T3_q), .Q2(T2_q), .Q1(T1_q), .Q0(T0_q), .X(X), .RESET(RST), .T3_NEXT_INPUT(t3_logic_1_t3_next_input));
  T_Flip_Flop T0 (.T(t0_logic_1_t0_next_input), .clk(CLK), .Q(T0_q));  // open: Qn, reset, preset
  T_Flip_Flop T1 (.T(t1_logic_1_t1_next_input), .clk(CLK), .Q(T1_q));  // open: Qn, reset, preset
  T_Flip_Flop T2 (.T(t2_logic_1_t2_next_input), .clk(CLK), .Q(T2_q));  // open: Qn, reset, preset
  T_Flip_Flop T3 (.T(t3_logic_1_t3_next_input), .clk(CLK), .Q(T3_q));  // open: Qn, reset, preset
  OUTPUT_LOGIC output_logic_1 (.Q3(T0_q), .Q2(T1_q), .Q1(T2_q), .Q0(T3_q), .CURR_OUTPUT(Z));

  // Notes on the sheet:
  //   Please put your deisgn below. You may also use subcircuits.
  //   However, do not move, rename, add, or delete any pins.
endmodule

module TB (
);

  wire clk_out, mypor_1_p2, not_1_out, or_1_out, RESET_out, TimeIndex_carry, undriven;
  wire [0:0] dut_1_z;
  wire [4:0] TimeIndex_q;

  Clock #(.highDuration(2), .lowDuration(2)) clk (.out(clk_out));
  Clock sysclk ();  // open: out
  Counter #(.max('h1f), .ongoal("stay"), .width(5)) TimeIndex (
    .load(or_1_out), .clk(clk_out), .D({5{1'b0}}), .carry(TimeIndex_carry), .Q(TimeIndex_q));  // open: clr, up, count
  // MyPOR mypor_1: pin names not known; wires that end beside it: clk_out, mypor_1_p2
  Button RESET (.out(RESET_out));
  ROM #(.addrWidth(5), .dataWidth(1)) TestTraceMemory (.addr(TimeIndex_q));  // open: data
  or or_1 (or_1_out, mypor_1_p2, RESET_out);
  not not_1 (not_1_out, TimeIndex_carry);
  DUT dut_1 (.X(undriven), .CLK(clk_out), .RST(or_1_out), .Z(dut_1_z[0]));
  TTY tty_1 (.data({6'b011000, dut_1_z[0]}), .clk(clk_out), .we(not_1_out), .clr(or_1_out));
  LED DONE (.in(TimeIndex_carry));

  // Notes on the sheet:
  //   DO NOT MODIFY THIS
  //   YOU MAY TEST YOUR CIRCUITS USING THIS TO MAKE SURE YOU HAVE NOT ALTERED PIN OUT
  //   Edit ROM with input trace of 32 bits
endmodule

module TBRANDOM (
);

  wire clk_out, mypor_1_p2, not_1_out, or_1_out, random_1_out, RESET_out, TimeIndex_carry;
  wire [0:0] dut_1_z;

  Clock #(.highDuration(2), .lowDuration(2)) clk (.out(clk_out));
  Clock sysclk ();  // open: out
  Counter #(.ongoal("stay")) TimeIndex (
    .load(or_1_out), .clk(clk_out), .D({8{1'b0}}), .carry(TimeIndex_carry));  // open: clr, up, count, Q
  // MyPOR mypor_1: pin names not known; wires that end beside it: clk_out, mypor_1_p2
  Button RESET (.out(RESET_out));
  or or_1 (or_1_out, mypor_1_p2, RESET_out);
  Random #(.width(1)) random_1 (.clr(or_1_out), .clk(clk_out), .out(random_1_out));  // open: next
  not not_1 (not_1_out, TimeIndex_carry);
  DUT dut_1 (.X(random_1_out), .CLK(clk_out), .RST(or_1_out), .Z(dut_1_z[0]));
  TTY tty_1 (.data({6'b011000, dut_1_z[0]}), .clk(clk_out), .we(not_1_out), .clr(or_1_out));
  LED DONE (.in(TimeIndex_carry));

  // Notes on the sheet:
  //   DO NOT MODIFY THIS
  //   YOU MAY TEST YOUR CIRCUITS USING THIS TO MAKE SURE YOU HAVE NOT ALTERED PIN OUT
endmodule

module AG_DONOTEDIT (
);

  // Rv32im rv32im_1: pin names not known
  ROM #(.addrWidth(5), .dataWidth(4)) FP ();  // open: addr, data

  // Notes on the sheet:
  //   contents of FP (hex, n*v repeats v):
  //   f 6 0 e 1 2 4 f 6 1 c 6 3 e b 0 f 5 f 7 e 7 a 2 9 7 5 8 f 5 7 a
  //   DO NOT MODIFY THIS
  //   THIS IS FOR AUTOGRADER'S USE - DO NOT TAMPER
endmodule

module AND4 (
  input  A,
  input  B,
  input  C,
  input  D,
  output SEN_ZEKKEN
);

  wire nand_1_out;

  nand nand_1 (nand_1_out, A, B, C, D);
  not not_1 (SEN_ZEKKEN, nand_1_out);
endmodule

module OR4 (
  input  A,
  input  B,
  input  C,
  input  D,
  output FPX
);

  wire not_1_out, not_2_out, not_3_out, not_4_out;

  not not_1 (not_1_out, A);
  not not_2 (not_2_out, B);
  not not_3 (not_3_out, C);
  not not_4 (not_4_out, D);
  nand nand_1 (FPX, not_1_out, not_2_out, not_3_out, not_4_out);
endmodule

module T3_LOGIC (
  input  Q3,
  input  Q2,
  input  Q1,
  input  Q0,
  input  X,
  input  RESET,
  output T3_NEXT_INPUT
);

  wire nand_1_out, nand_2_out, nand_3_out, nand_4_out, nand_5_out, nand_6_out, nand_7_out, nand_8_out,
       nand_9_out, nand_10_out, nand_11_out, not_1_out, not_2_out, not_3_out, not_4_out, not_5_out,
       not_6_out, not_7_out, not_8_out, or2_1_demon1;

  not not_1 (not_1_out, Q1);
  not not_2 (not_2_out, Q2);
  not not_3 (not_3_out, Q0);
  not not_4 (not_4_out, X);
  nand nand_1 (nand_1_out, Q1, Q3);
  nand nand_2 (nand_2_out, Q0, Q1);
  nand nand_3 (nand_3_out, Q2, not_1_out);
  nand nand_4 (nand_4_out, not_2_out, Q3);
  not not_5 (not_5_out, nand_1_out);
  nand nand_5 (nand_5_out, not_4_out, Q2);
  not not_6 (not_6_out, nand_2_out);
  not not_7 (not_7_out, nand_4_out);
  nand nand_6 (nand_6_out, X, not_5_out);
  nand nand_7 (nand_7_out, nand_6_out, nand_5_out);
  nand nand_8 (nand_8_out, not_6_out, not_7_out);
  nand nand_9 (nand_9_out, not_3_out, nand_7_out);
  XOR2 xor2_1 (.IN1(Q3), .IN2(or2_1_demon1), .SUMMIT(T3_NEXT_INPUT));
  nand nand_10 (nand_10_out, nand_8_out, nand_9_out);
  not not_8 (not_8_out, nand_10_out);
  nand nand_11 (nand_11_out, not_8_out, nand_3_out);
  OR2 or2_1 (.INPUT1(nand_11_out), .INPUT2(RESET), .DEMON1(or2_1_demon1));
endmodule

module T1_LOGIC (
  input  Q3,
  input  Q2,
  input  Q1,
  input  Q0,
  input  X,
  input  RESET,
  output T1_NEXT_INPUT
);

  wire nand_1_out, nand_2_out, nand_3_out, nand_4_out, nand_5_out, nand_6_out, nand_7_out, nand_8_out,
       nand_9_out, not_1_out, not_2_out, not_3_out, not_4_out, not_5_out, not_6_out, not_7_out, or2_1_demon1;

  not not_1 (not_1_out, Q3);
  not not_2 (not_2_out, Q2);
  not not_3 (not_3_out, Q1);
  not not_4 (not_4_out, Q0);
  not not_5 (not_5_out, X);
  nand nand_1 (nand_1_out, not_5_out, Q3);
  nand nand_2 (nand_2_out, not_1_out, X);
  nand nand_3 (nand_3_out, not_3_out, Q2);
  not not_6 (not_6_out, nand_1_out);
  nand nand_4 (nand_4_out, not_2_out, nand_1_out);
  nand nand_5 (nand_5_out, not_4_out, not_6_out);
  nand nand_6 (nand_6_out, nand_4_out, nand_3_out);
  not not_7 (not_7_out, nand_6_out);
  nand nand_7 (nand_7_out, not_7_out, nand_2_out);
  nand nand_8 (nand_8_out, Q0, nand_7_out);
  OR2 or2_1 (.INPUT1(nand_9_out), .INPUT2(RESET), .DEMON1(or2_1_demon1));
  nand nand_9 (nand_9_out, nand_5_out, nand_8_out);
  XOR2 xor2_1 (.IN1(Q1), .IN2(or2_1_demon1), .SUMMIT(T1_NEXT_INPUT));
endmodule

module T2_LOGIC (
  input  Q3,
  input  Q2,
  input  Q1,
  input  Q0,
  input  X,
  input  RESET,
  output T2_NEXT_INPUT
);

  wire nand_1_out, nand_2_out, nand_3_out, nand_4_out, nand_5_out, nand_6_out, nand_7_out, not_1_out,
       not_2_out, not_3_out, not_4_out, not_5_out, not_6_out, or2_1_demon1;

  not not_1 (not_1_out, Q3);
  not not_2 (not_2_out, Q2);
  not not_3 (not_3_out, Q1);
  not not_4 (not_4_out, Q0);
  not not_5 (not_5_out, X);
  nand nand_1 (nand_1_out, not_2_out, not_1_out);
  nand nand_2 (nand_2_out, not_3_out, Q3);
  nand nand_3 (nand_3_out, not_4_out, not_5_out);
  not not_6 (not_6_out, nand_2_out);
  nand nand_4 (nand_4_out, nand_3_out, nand_1_out);
  nand nand_5 (nand_5_out, nand_3_out, not_6_out);
  nand nand_6 (nand_6_out, nand_4_out, Q1);
  XOR2 xor2_1 (.IN1(Q2), .IN2(or2_1_demon1), .SUMMIT(T2_NEXT_INPUT));
  nand nand_7 (nand_7_out, nand_5_out, nand_6_out);
  OR2 or2_1 (.INPUT1(nand_7_out), .INPUT2(RESET), .DEMON1(or2_1_demon1));
endmodule

module T0_LOGIC (
  input  Q3,
  input  Q2,
  input  Q1,
  input  Q0,
  input  X,
  input  RESET,
  output T0_NEXT_INPUT
);

  wire nand_1_out, nand_2_out, nand_3_out, nand_4_out, nand_5_out, nand_6_out, nand_7_out, nand_8_out,
       nand_9_out, nand_10_out, nand_11_out, nand_12_out, nand_13_out, not_1_out, not_2_out, not_3_out,
       not_4_out, not_5_out, or2_1_demon1;

  not not_1 (not_1_out, X);
  not not_2 (not_2_out, Q3);
  nand nand_1 (nand_1_out, Q2, X);
  nand nand_2 (nand_2_out, Q1, Q2);
  nand nand_3 (nand_3_out, Q0, Q2);
  not not_3 (not_3_out, nand_1_out);
  not not_4 (not_4_out, nand_3_out);
  nand nand_4 (nand_4_out, not_1_out, Q1);
  nand nand_5 (nand_5_out, X, nand_2_out);
  not not_5 (not_5_out, nand_4_out);
  nand nand_6 (nand_6_out, Q0, not_3_out);
  nand nand_7 (nand_7_out, not_1_out, nand_3_out);
  nand nand_8 (nand_8_out, not_4_out, not_5_out);
  nand nand_9 (nand_9_out, nand_7_out, nand_6_out);
  nand nand_10 (nand_10_out, nand_8_out, nand_5_out);
  nand nand_11 (nand_11_out, Q3, nand_9_out);
  nand nand_12 (nand_12_out, not_2_out, nand_10_out);
  nand nand_13 (nand_13_out, nand_11_out, nand_12_out);
  OR2 or2_1 (.INPUT1(RESET), .INPUT2(nand_13_out), .DEMON1(or2_1_demon1));
  XOR2 xor2_1 (.IN1(Q0), .IN2(or2_1_demon1), .SUMMIT(T0_NEXT_INPUT));
endmodule

module AND5 (
  input  IN1,
  input  IN2,
  input  IN3,
  input  IN4,
  input  IN5,
  output G2_ESPORTS
);

  wire nand_1_out;

  nand nand_1 (nand_1_out, IN1, IN2, IN3, IN4, IN5);
  not not_1 (G2_ESPORTS, nand_1_out);
endmodule

module OR8 (
  input  IN1,
  input  IN2,
  input  IN3,
  input  IN4,
  input  IN5,
  input  IN6,
  input  IN7,
  input  IN8,
  output WOAIZHONGGUOCAI
);

  wire not_1_out, not_2_out, not_3_out, not_4_out, not_5_out, not_6_out, not_7_out, not_8_out;

  not not_1 (not_1_out, IN1);
  not not_2 (not_2_out, IN2);
  not not_3 (not_3_out, IN3);
  not not_4 (not_4_out, IN4);
  not not_5 (not_5_out, IN5);
  not not_6 (not_6_out, IN6);
  not not_7 (not_7_out, IN7);
  not not_8 (not_8_out, IN8);
  nand nand_1 (WOAIZHONGGUOCAI, not_1_out, not_2_out, not_3_out, not_4_out, not_5_out, not_6_out, not_7_out, not_8_out);
endmodule

module XOR2 (
  input  IN1,
  input  IN2,
  output SUMMIT
);

  wire nand_1_out, nand_2_out, not_1_out, not_2_out;

  not not_1 (not_1_out, IN1);
  not not_2 (not_2_out, IN2);
  nand nand_1 (nand_1_out, IN1, not_2_out);
  nand nand_2 (nand_2_out, not_1_out, IN2);
  nand nand_3 (SUMMIT, nand_1_out, nand_2_out);
endmodule

module OR2 (
  input  INPUT1,
  input  INPUT2,
  output DEMON1
);

  wire not_1_out, not_2_out;

  not not_1 (not_1_out, INPUT1);
  not not_2 (not_2_out, INPUT2);
  nand nand_1 (DEMON1, not_1_out, not_2_out);
endmodule

module OUTPUT_LOGIC (
  input  Q3,
  input  Q2,
  input  Q1,
  input  Q0,
  output CURR_OUTPUT
);

  wire not_1_out, not_2_out, not_3_out, not_4_out;

  not not_1 (not_1_out, Q3);
  not not_2 (not_2_out, Q2);
  not not_3 (not_3_out, Q1);
  not not_4 (not_4_out, Q0);
  AND4 and4_1 (.A(not_1_out), .B(not_2_out), .C(not_3_out), .D(not_4_out), .SEN_ZEKKEN(CURR_OUTPUT));
endmodule

module T2_LOGIC_COPY (
  input  Q3,
  input  Q2,
  input  Q1,
  input  Q0,
  input  X,
  input  RESET,
  output T2_NEXT_INPUT
);

  wire and3_1_sen_zekken, and3_2_sen_zekken, and3_3_sen_zekken, and3_4_sen_zekken, not_1_out, not_2_out,
       not_3_out, not_4_out, not_5_out, or4_1_fpx;

  not not_1 (not_1_out, Q3);
  not not_2 (not_2_out, Q2);
  not not_3 (not_3_out, Q1);
  not not_4 (not_4_out, Q0);
  not not_5 (not_5_out, X);
  AND3 and3_1 (.A(not_1_out), .B(not_2_out), .C(Q1), .SEN_ZEKKEN(and3_1_sen_zekken));
  AND3 and3_2 (.A(Q3), .B(not_3_out), .C(X), .SEN_ZEKKEN(and3_2_sen_zekken));
  AND3 and3_3 (.A(Q3), .B(not_3_out), .C(Q0), .SEN_ZEKKEN(and3_3_sen_zekken));
  AND3 and3_4 (.A(Q1), .B(not_4_out), .C(not_5_out), .SEN_ZEKKEN(and3_4_sen_zekken));
  OR4 or4_1 (
    .A(and3_1_sen_zekken), .B(and3_2_sen_zekken), .C(and3_3_sen_zekken), .D(and3_4_sen_zekken),
    .FPX(or4_1_fpx));
  OR2 or2_1 (.INPUT1(RESET), .INPUT2(or4_1_fpx), .DEMON1(T2_NEXT_INPUT));
endmodule

module AND3 (
  input  A,
  input  B,
  input  C,
  output SEN_ZEKKEN
);

  wire nand_1_out;

  nand nand_1 (nand_1_out, A, B, C);
  not not_1 (SEN_ZEKKEN, nand_1_out);
endmodule
