// Logisim project da1_task1.circ as structural Verilog: 6 circuits, main circuit DUT
module DUT (
  input  X11,
  input  X12,
  input  X13,
  input  X21,
  input  X22,
  input  X23,
  input  X31,
  input  X32,
  input  X33,
  output F
);

  \final  final_1 (
    .X11(X11), .X12(X12), .X13(X13), .X21(X21), .X22(X22), .X23(X23), .X31(X31), .X32(X32), .X33(X33), .F(F));

  // Notes on the sheet:
  //   Please put your deisgn below. You may also use subcircuits.
  //   However, do not add or delete or move or rename any pins.
endmodule

module TB (
  input  X11,
  input  X12,
  input  X13,
  input  X21,
  input  X22,
  input  X23,
  input  X31,
  input  X32,
  input  X33,
  output F
);

  DUT dut_1 (.X11(X11), .X12(X12), .X13(X13), .X21(X21), .X22(X22), .X23(X23), .X31(X31), .X32(X32), .X33(X33), .F(F));

  // Notes on the sheet:
  //   DO NOT MODIFY THIS
  //   TEST YOUR CIRCUITS USING THIS TO MAKE SURE YOU HAVE NOT ALTERED PIN OUT
endmodule

module AG_DONOTEDIT (
);

  // Rv32im rv32im_1: pin names not known
  ROM #(.addrWidth(5), .dataWidth(4)) FP ();  // open: addr, data

  // Notes on the sheet:
  //   contents of FP (hex, n*v repeats v):
  //   f 6 0 e 1 2 4 f 6 1 c 6 3 e b 0 f 5 f 7 e 7 a 2 9 7 5 8 f 5 7 a
  //   DO NOT MODIFY THIS
  //   THIS IS FOR AUTOGRADER'S USE - DO NOT TAMPER
endmodule

module check2 (
  input  A,
  input  B,
  output F
);

  nand nand_1 (F, A, B);

  // Notes on the sheet:
  //   1 = SUCCESS, 0 = FAIL
endmodule

module check3 (
  input  A,
  input  B,
  input  C,
  output F
);

  wire nand_1_out, nand_2_out, nand_3_out, nand_4_out;

  nand nand_1 (nand_1_out, A, B);
  nand nand_2 (nand_2_out, B, C);
  nand nand_3 (nand_3_out, A, C);
  nand nand_4 (nand_4_out, nand_1_out, nand_2_out, nand_3_out);
  not not_1 (F, nand_4_out);

  // Notes on the sheet:
  //   1 = SUCCESS, 0 = FAIL
endmodule

module \final  (
  input  X11,
  input  X12,
  input  X13,
  input  X21,
  input  X22,
  input  X23,
  input  X31,
  input  X32,
  input  X33,
  output F
);

  wire check2_1_f, check2_2_f, check2_3_f, check2_4_f, check3_1_f, check3_2_f, check3_3_f, check3_4_f,
       check3_5_f, check3_6_f, check3_7_f, check3_8_f, nand_1_out;

  check3 check3_1 (.A(X11), .B(X12), .C(X13), .F(check3_1_f));
  check3 check3_2 (.A(X21), .B(X22), .C(X23), .F(check3_2_f));
  check3 check3_3 (.A(X31), .B(X32), .C(X33), .F(check3_3_f));
  check3 check3_4 (.A(X11), .B(X21), .C(X31), .F(check3_4_f));
  check3 check3_5 (.A(X12), .B(X22), .C(X32), .F(check3_5_f));
  check3 check3_6 (.A(X13), .B(X23), .C(X33), .F(check3_6_f));
  check3 check3_7 (.A(X11), .B(X22), .C(X33), .F(check3_7_f));
  check3 check3_8 (.A(X13), .B(X22), .C(X31), .F(check3_8_f));
  check2 check2_1 (.A(X12), .B(X23), .F(check2_1_f));
  check2 check2_2 (.A(X21), .B(X32), .F(check2_2_f));
  check2 check2_3 (.A(X12), .B(X21), .F(check2_3_f));
  check2 check2_4 (.A(X23), .B(X32), .F(check2_4_f));
  nand nand_1 (nand_1_out, check3_1_f, check3_2_f, check3_3_f, check3_4_f, check3_5_f, check3_6_f, check3_7_f, check3_8_f, check2_1_f, check2_2_f, check2_3_f, check2_4_f);
  not not_1 (F, nand_1_out);

  // Notes on the sheet:
  //   rows
  //   columns
  //   big diagonals
  //   small diagonals
  //   inverted results
endmodule
