// Logisim project da1_task4.circ as structural Verilog: 5 circuits, main circuit DUT
module DUT (
  input  [1:0] S0,
  input  [1:0] S1,
  input  [1:0] S2,
  input  [1:0] S3,
  input  [1:0] S4,
  input  [1:0] S5,
  input  [1:0] S6,
  input  [1:0] S7,
  output [1:0] DOUT,
  output [2:0] SID
);

  \final  final_1 (.S0(S0), .S1(S1), .S2(S2), .S3(S3), .S4(S4), .S5(S5), .S6(S6), .S7(S7), .DOUT(DOUT), .SID(SID));

  // Notes on the sheet:
  //   Please put your design below. You may also use subcircuits.
  //   However, do not move, rename, add, or delete any pins.
endmodule

module TB (
  input  [1:0] S0,
  input  [1:0] S1,
  input  [1:0] S2,
  input  [1:0] S3,
  input  [1:0] S4,
  input  [1:0] S5,
  input  [1:0] S6,
  input  [1:0] S7,
  output [1:0] DOUT,
  output [2:0] SID
);

  DUT dut_1 (.S0(S0), .S1(S1), .S2(S2), .S3(S3), .S4(S4), .S5(S5), .S6(S6), .S7(S7), .DOUT(DOUT), .SID(SID));

  // Notes on the sheet:
  //   Please put your deisgn below. You may also use subcircuits.
  //   However, do not move or rename any pins.
endmodule

module AG_DONOTEDIT (
);

  // Rv32im rv32im_1: pin names not known
  ROM #(.addrWidth(5), .dataWidth(4)) FP ();  // open: addr, data

  // Notes on the sheet:
  //   contents of FP (hex, n*v repeats v):
  //   f 6 0 e 1 2 4 f 6 1 c 6 3 e b 0 f 5 f 7 e 7 a 2 9 7 5 8 f 5 7 a
  //   DO NOT MODIFY THIS
  //   THIS IS FOR AUTOGRADER'S USE - DO NOT TAMPER
endmodule

module checkNot00 (
  input  [1:0] A,
  output O
);

  // OR_Gate or_1 has open pins: out=O
endmodule

module \final  (
  input  [1:0] S0,
  input  [1:0] S1,
  input  [1:0] S2,
  input  [1:0] S3,
  input  [1:0] S4,
  input  [1:0] S5,
  input  [1:0] S6,
  input  [1:0] S7,
  output [1:0] DOUT,
  output [2:0] SID
);

  wire checknot00_1_o, checknot00_2_o, checknot00_3_o, checknot00_4_o, checknot00_5_o, checknot00_6_o,
       checknot00_7_o, checknot00_8_o, priority_encoder_1_en_out;
  wire [2:0] bit_extender_1_out, not_1_out, priority_encoder_1_out;

  checkNot00 checknot00_1 (.A(S0), .O(checknot00_1_o));
  checkNot00 checknot00_2 (.A(S1), .O(checknot00_2_o));
  checkNot00 checknot00_3 (.A(S2), .O(checknot00_3_o));
  checkNot00 checknot00_4 (.A(S3), .O(checknot00_4_o));
  checkNot00 checknot00_5 (.A(S4), .O(checknot00_5_o));
  checkNot00 checknot00_6 (.A(S5), .O(checknot00_6_o));
  checkNot00 checknot00_7 (.A(S6), .O(checknot00_7_o));
  checkNot00 checknot00_8 (.A(S7), .O(checknot00_8_o));
  assign bit_extender_1_out = {{2{priority_encoder_1_en_out}}, priority_encoder_1_en_out};  // Bit_Extender bit_extender_1
  Priority_Encoder priority_encoder_1 (
    .in0(checknot00_8_o), .in1(checknot00_7_o), .in2(checknot00_6_o), .in3(checknot00_5_o),
    .in4(checknot00_4_o), .in5(checknot00_3_o), .in6(checknot00_2_o), .in7(checknot00_1_o),
    .out(priority_encoder_1_out), .en_out(priority_encoder_1_en_out));  // open: en_in, gs
  assign not_1_out = ~bit_extender_1_out;  // NOT_Gate not_1, 3 bits wide
  Multiplexer #(.select(3), .width(2)) multiplexer_1 (
    .in0(S0), .in1(S1), .in2(S2), .in3(S3), .in4(S4), .in5(S5), .in6(S6), .in7(S7), .out(DOUT), .sel(SID));
  assign SID = ~(not_1_out & priority_encoder_1_out);  // NAND_Gate nand_1, 3 bits wide
endmodule
