// Logisim project da1_task1.circ as structural Verilog: 3 circuits, main circuit DUT
module DUT (
  input  X11,
  input  X12,
  input  X13,
  input  X21,
  input  X22,
  input  X23,
  input  X31,
  input  X32,
  input  X33,
  output F
);


  // Notes on the sheet:
  //   Please put your deisgn below. You may also use subcircuits.
  //   However, do not add or delete or move or rename any pins.
endmodule

module TB (
  input  X11,
  input  X12,
  input  X13,
  input  X21,
  input  X22,
  input  X23,
  input  X31,
  input  X32,
  input  X33,
  output F
);

  DUT dut_1 (.X11(X11), .X12(X12), .X13(X13), .X21(X21), .X22(X22), .X23(X23), .X31(X31), .X32(X32), .X33(X33), .F(F));

  // Notes on the sheet:
  //   DO NOT MODIFY THIS
  //   TEST YOUR CIRCUITS USING THIS TO MAKE SURE YOU HAVE NOT ALTERED PIN OUT
endmodule

module AG_DONOTEDIT (
);

  // Rv32im rv32im_1: pin names not known
  ROM #(.addrWidth(5), .dataWidth(4)) FP ();  // open: addr, data

  // Notes on the sheet:
  //   contents of FP (hex, n*v repeats v):
  //   f 6 0 e 1 2 4 f 6 1 c 6 3 e b 0 f 5 f 7 e 7 a 2 9 7 5 8 f 5 7 a
  //   DO NOT MODIFY THIS
  //   THIS IS FOR AUTOGRADER'S USE - DO NOT TAMPER
endmodule
