// Logisim project da1_task2.circ as structural Verilog: 6 circuits, main circuit DUT
module DUT (
  input  IS_SIGNED,
  input  [7:0] D0,
  input  [7:0] D1,
  input  [7:0] D2,
  output [7:0] H,
  output [7:0] M,
  output [7:0] L
);

  wire [8:0] hml3signed_1_max, hml3signed_1_mid, hml3signed_1_min, signbit_1_out_3, signbit_2_out_3,
       signbit_3_out_3;

  signBit signbit_1 (.SIGN_BIT(IS_SIGNED), .INITIAL_INPUT(D0), .out_3(signbit_1_out_3));
  signBit signbit_2 (.SIGN_BIT(IS_SIGNED), .INITIAL_INPUT(D1), .out_3(signbit_2_out_3));
  signBit signbit_3 (.SIGN_BIT(IS_SIGNED), .INITIAL_INPUT(D2), .out_3(signbit_3_out_3));
  hML3Signed hml3signed_1 (
    .A(signbit_1_out_3), .B(signbit_2_out_3), .C(signbit_3_out_3), .max(hml3signed_1_max),
    .mid(hml3signed_1_mid), .min(hml3signed_1_min));
  Bit_Extender #(.in_width(9), .out_width(8)) bit_extender_1 (.in(hml3signed_1_max), .out(H));
  Bit_Extender #(.in_width(9), .out_width(8)) bit_extender_2 (.in(hml3signed_1_mid), .out(M));
  Bit_Extender #(.in_width(9), .out_width(8)) bit_extender_3 (.in(hml3signed_1_min), .out(L));

  // Notes on the sheet:
  //   Please put your deisgn below. You may also use subcircuits.
  //   However, do not move or rename any pins.
endmodule

module TB (
  input  IS_SIGNED,
  input  [7:0] D0,
  input  [7:0] D1,
  input  [7:0] D3,
  output [7:0] H,
  output [7:0] M,
  output [7:0] L
);

  DUT dut_1 (.IS_SIGNED(IS_SIGNED), .D0(D0), .D1(D1), .D2(D3), .H(H), .M(M), .L(L));

  // Notes on the sheet:
  //   DO NOT MODIFY THIS
  //   TEST YOUR CIRCUITS USING THIS TO MAKE SURE YOU HAVE NOT ALTERED PIN OUT
endmodule

module AG_DONOTEDIT (
);

  // Rv32im rv32im_1: pin names not known
  ROM #(.addrWidth(5), .dataWidth(4)) FP ();  // open: addr, data

  // Notes on the sheet:
  //   contents of FP (hex, n*v repeats v):
  //   f 6 0 e 1 2 4 f 6 1 c 6 3 e b 0 f 5 f 7 e 7 a 2 9 7 5 8 f 5 7 a
  //   DO NOT MODIFY THIS
  //   THIS IS FOR AUTOGRADER'S USE - DO NOT TAMPER
endmodule

module hML3Unsigned (
  input  [7:0] A,
  input  [7:0] B,
  input  [7:0] C,
  output [7:0] MAX,
  output [7:0] MID,
  output [7:0] MIN
);

  wire comparator_1_lt, comparator_2_lt, comparator_3_gt, comparator_3_lt;
  wire [7:0] multiplexer_1_out, multiplexer_3_out, multiplexer_4_out, multiplexer_7_out;

  Comparator #(.mode("unsigned")) comparator_1 (.a(A), .b(B), .lt(comparator_1_lt));  // open: gt, eq
  Multiplexer #(.width(8)) multiplexer_1 (.in0(A), .in1(B), .out(multiplexer_1_out), .sel(comparator_1_lt));
  Comparator #(.mode("unsigned")) comparator_2 (.a(multiplexer_1_out), .b(C), .lt(comparator_2_lt));  // open: gt, eq
  Multiplexer #(.width(8)) multiplexer_2 (.in0(multiplexer_1_out), .in1(C), .out(MAX), .sel(comparator_2_lt));
  Multiplexer #(.width(8)) multiplexer_3 (.in0(B), .in1(A), .out(multiplexer_3_out), .sel(comparator_1_lt));
  Multiplexer #(.width(8)) multiplexer_4 (
    .in0(multiplexer_3_out), .in1(multiplexer_1_out), .out(multiplexer_4_out), .sel(comparator_2_lt));
  Comparator #(.mode("unsigned")) comparator_3 (
    .a(multiplexer_3_out), .b(C), .gt(comparator_3_gt), .lt(comparator_3_lt));  // open: eq
  Multiplexer #(.width(8)) multiplexer_5 (
    .in0(multiplexer_4_out), .in1(multiplexer_7_out), .out(MID), .sel(comparator_3_lt));
  Multiplexer #(.width(8)) multiplexer_6 (.in0(multiplexer_3_out), .in1(C), .out(MIN), .sel(comparator_3_gt));
  Multiplexer #(.width(8)) multiplexer_7 (
    .in0(C), .in1(multiplexer_1_out), .out(multiplexer_7_out), .sel(comparator_2_lt));

  // Notes on the sheet:
  //   max(A,B)
  //   min(A,B)
endmodule

module hML3Signed (
  input  [8:0] A,
  input  [8:0] B,
  input  [8:0] C,
  output [8:0] max,
  output [8:0] mid,
  output [8:0] min
);

  wire comparator_1_lt, comparator_2_lt, comparator_3_gt, comparator_3_lt;
  wire [8:0] multiplexer_1_out, multiplexer_3_out, multiplexer_4_out, multiplexer_7_out;

  Comparator #(.width(9)) comparator_1 (.a(A), .b(B), .lt(comparator_1_lt));  // open: gt, eq
  Multiplexer #(.width(9)) multiplexer_1 (.in0(A), .in1(B), .out(multiplexer_1_out), .sel(comparator_1_lt));
  Comparator #(.width(9)) comparator_2 (.a(multiplexer_1_out), .b(C), .lt(comparator_2_lt));  // open: gt, eq
  Multiplexer #(.width(9)) multiplexer_2 (.in0(multiplexer_1_out), .in1(C), .out(max), .sel(comparator_2_lt));
  Multiplexer #(.width(9)) multiplexer_3 (.in0(B), .in1(A), .out(multiplexer_3_out), .sel(comparator_1_lt));
  Multiplexer #(.width(9)) multiplexer_4 (
    .in0(multiplexer_3_out), .in1(multiplexer_1_out), .out(multiplexer_4_out), .sel(comparator_2_lt));
  Comparator #(.width(9)) comparator_3 (
    .a(multiplexer_3_out), .b(C), .gt(comparator_3_gt), .lt(comparator_3_lt));  // open: eq
  Multiplexer #(.width(9)) multiplexer_5 (
    .in0(multiplexer_4_out), .in1(multiplexer_7_out), .out(mid), .sel(comparator_3_lt));
  Multiplexer #(.width(9)) multiplexer_6 (.in0(multiplexer_3_out), .in1(C), .out(min), .sel(comparator_3_gt));
  Multiplexer #(.width(9)) multiplexer_7 (
    .in0(C), .in1(multiplexer_1_out), .out(multiplexer_7_out), .sel(comparator_2_lt));

  // Notes on the sheet:
  //   max(A,B)
  //   min(A,B)
endmodule

module signBit (
  input  SIGN_BIT,
  input  [7:0] INITIAL_INPUT,
  output [8:0] out_3
);

  wire [8:0] bit_extender_1_out, nand_1_out, not_1_out;

  assign bit_extender_1_out = {{1{INITIAL_INPUT[7]}}, INITIAL_INPUT};  // Bit_Extender bit_extender_1
  assign nand_1_out = ~(bit_extender_1_out & 9'hff);  // NAND_Gate nand_1, 9 bits wide
  assign not_1_out = ~nand_1_out;  // NOT_Gate not_1, 9 bits wide
  Multiplexer #(.width(9)) multiplexer_1 (.in0(not_1_out), .in1(bit_extender_1_out), .out(out_3), .sel(SIGN_BIT));
endmodule
