// Logisim project da1_task3.circ as structural Verilog: 4 circuits, main circuit DUT
module DUT (
  input  [6:0] A,
  output [63:0] B_LOWER,
  output [63:0] B_UPPER
);

  wire decoder_1_out0, decoder_1_out1, decoder_1_out2, decoder_1_out3;

  Decoder #(.select(2)) decoder_1 (
    .out0(decoder_1_out0), .out1(decoder_1_out1), .out2(decoder_1_out2), .out3(decoder_1_out3), .sel(A[6:5]));  // open: en
  Decoder #(.select(5)) decoder_2 (
    .out0(B_LOWER[0]), .out1(B_LOWER[1]), .out2(B_LOWER[2]), .out3(B_LOWER[3]), .out4(B_LOWER[4]),
    .out5(B_LOWER[5]), .out6(B_LOWER[6]), .out7(B_LOWER[7]), .out8(B_LOWER[8]), .out9(B_LOWER[9]),
    .out10(B_LOWER[10]), .out11(B_LOWER[11]), .out12(B_LOWER[12]), .out13(B_LOWER[13]), .out14(B_LOWER[14]),
    .out15(B_LOWER[15]), .out16(B_LOWER[16]), .out17(B_LOWER[17]), .out18(B_LOWER[18]), .out19(B_LOWER[19]),
    .out20(B_LOWER[20]), .out21(B_LOWER[21]), .out22(B_LOWER[22]), .out23(B_LOWER[23]), .out24(B_LOWER[24]),
    .out25(B_LOWER[25]), .out26(B_LOWER[26]), .out27(B_LOWER[27]), .out28(B_LOWER[28]), .out29(B_LOWER[29]),
    .out30(B_LOWER[30]), .out31(B_LOWER[31]), .sel(A[4:0]), .en(decoder_1_out0));
  Decoder #(.select(5)) decoder_3 (
    .out0(B_LOWER[32]), .out1(B_LOWER[33]), .out2(B_LOWER[34]), .out3(B_LOWER[35]), .out4(B_LOWER[36]),
    .out5(B_LOWER[37]), .out6(B_LOWER[38]), .out7(B_LOWER[39]), .out8(B_LOWER[40]), .out9(B_LOWER[41]),
    .out10(B_LOWER[42]), .out11(B_LOWER[43]), .out12(B_LOWER[44]), .out13(B_LOWER[45]), .out14(B_LOWER[46]),
    .out15(B_LOWER[47]), .out16(B_LOWER[48]), .out17(B_LOWER[49]), .out18(B_LOWER[50]), .out19(B_LOWER[51]),
    .out20(B_LOWER[52]), .out21(B_LOWER[53]), .out22(B_LOWER[54]), .out23(B_LOWER[55]), .out24(B_LOWER[56]),
    .out25(B_LOWER[57]), .out26(B_LOWER[58]), .out27(B_LOWER[59]), .out28(B_LOWER[60]), .out29(B_LOWER[61]),
    .out30(B_LOWER[62]), .out31(B_LOWER[63]), .sel(A[4:0]), .en(decoder_1_out1));
  Decoder #(.select(5)) decoder_4 (
    .out0(B_UPPER[0]), .out1(B_UPPER[1]), .out2(B_UPPER[2]), .out3(B_UPPER[3]), .out4(B_UPPER[4]),
    .out5(B_UPPER[5]), .out6(B_UPPER[6]), .out7(B_UPPER[7]), .out8(B_UPPER[8]), .out9(B_UPPER[9]),
    .out10(B_UPPER[10]), .out11(B_UPPER[11]), .out12(B_UPPER[12]), .out13(B_UPPER[13]), .out14(B_UPPER[14]),
    .out15(B_UPPER[15]), .out16(B_UPPER[16]), .out17(B_UPPER[17]), .out18(B_UPPER[18]), .out19(B_UPPER[19]),
    .out20(B_UPPER[20]), .out21(B_UPPER[21]), .out22(B_UPPER[22]), .out23(B_UPPER[23]), .out24(B_UPPER[24]),
    .out25(B_UPPER[25]), .out26(B_UPPER[26]), .out27(B_UPPER[27]), .out28(B_UPPER[28]), .out29(B_UPPER[29]),
    .out30(B_UPPER[30]), .out31(B_UPPER[31]), .sel(A[4:0]), .en(decoder_1_out2));
  Decoder #(.select(5)) decoder_5 (
    .out0(B_UPPER[32]), .out1(B_UPPER[33]), .out2(B_UPPER[34]), .out3(B_UPPER[35]), .out4(B_UPPER[36]),
    .out5(B_UPPER[37]), .out6(B_UPPER[38]), .out7(B_UPPER[39]), .out8(B_UPPER[40]), .out9(B_UPPER[41]),
    .out10(B_UPPER[42]), .out11(B_UPPER[43]), .out12(B_UPPER[44]), .out13(B_UPPER[45]), .out14(B_UPPER[46]),
    .out15(B_UPPER[47]), .out16(B_UPPER[48]), .out17(B_UPPER[49]), .out18(B_UPPER[50]), .out19(B_UPPER[51]),
    .out20(B_UPPER[52]), .out21(B_UPPER[53]), .out22(B_UPPER[54]), .out23(B_UPPER[55]), .out24(B_UPPER[56]),
    .out25(B_UPPER[57]), .out26(B_UPPER[58]), .out27(B_UPPER[59]), .out28(B_UPPER[60]), .out29(B_UPPER[61]),
    .out30(B_UPPER[62]), .out31(B_UPPER[63]), .sel(A[4:0]), .en(decoder_1_out3));

  // Notes on the sheet:
  //   Please put your deisgn below. You may also use subcircuits.
  //   However, do not move, rename, add, or delete any pins.
endmodule

module TB (
  input  [6:0] A,
  output [63:0] A_UPPER,
  output [63:0] A_LOWER
);

  DUT dut_1 (.A(A), .B_LOWER(A_UPPER), .B_UPPER(A_LOWER));

  // Notes on the sheet:
  //   Please put your deisgn below. You may also use subcircuits.
  //   However, do not move or rename any pins.
endmodule

module AG_DONOTEDIT (
);

  // Rv32im rv32im_1: pin names not known
  ROM #(.addrWidth(5), .dataWidth(4)) FP ();  // open: addr, data

  // Notes on the sheet:
  //   contents of FP (hex, n*v repeats v):
  //   f 6 0 e 1 2 4 f 6 1 c 6 3 e b 0 f 5 f 7 e 7 a 2 9 7 5 8 f 5 7 a
  //   DO NOT MODIFY THIS
  //   THIS IS FOR AUTOGRADER'S USE - DO NOT TAMPER
endmodule

module BUDGET_AND_GATE (
  input  A,
  input  B,
  input  C,
  output AND_OUTPUT
);

  wire nand_1_out;

  nand nand_1 (nand_1_out, A, B, C);
  not not_1 (AND_OUTPUT, nand_1_out);
endmodule
