// Logisim project da1_task4.circ as structural Verilog: 3 circuits, main circuit DUT
module DUT (
  input  [1:0] S0,
  input  [1:0] S1,
  input  [1:0] S2,
  input  [1:0] S3,
  input  [1:0] S4,
  input  [1:0] S5,
  input  [1:0] S6,
  input  [1:0] S7,
  output [1:0] DOUT,
  output [2:0] SID
);


  // Notes on the sheet:
  //   Please put your design below. You may also use subcircuits.
  //   However, do not move, rename, add, or delete any pins.
endmodule

module TB (
  input  [1:0] S0,
  input  [1:0] S1,
  input  [1:0] S2,
  input  [1:0] S3,
  input  [1:0] S4,
  input  [1:0] S5,
  input  [1:0] S6,
  input  [1:0] S7,
  output [1:0] DOUT,
  output [2:0] SID
);

  DUT dut_1 (.S0(S0), .S1(S1), .S2(S2), .S3(S3), .S4(S4), .S5(S5), .S6(S6), .S7(S7), .DOUT(DOUT), .SID(SID));

  // Notes on the sheet:
  //   Please put your deisgn below. You may also use subcircuits.
  //   However, do not move or rename any pins.
endmodule

module AG_DONOTEDIT (
);

  // Rv32im rv32im_1: pin names not known
  ROM #(.addrWidth(5), .dataWidth(4)) FP ();  // open: addr, data

  // Notes on the sheet:
  //   contents of FP (hex, n*v repeats v):
  //   f 6 0 e 1 2 4 f 6 1 c 6 3 e b 0 f 5 f 7 e 7 a 2 9 7 5 8 f 5 7 a
  //   DO NOT MODIFY THIS
  //   THIS IS FOR AUTOGRADER'S USE - DO NOT TAMPER
endmodule
